# Fritzing sketch S3X_Client (saved by Fritzing 0.9.3b)
breadboards: 2

parts:
  RCWL-0516 = PIR sensor
  元件1 = LCD1602-I2C
  S1 = Momentary Switch [package=ksa_sealed_tac_switch]
  C1815 = NPN-Transistor [package="SOT-23 [SMD]"]
  WeMos_D1_Mini1 = WeMos D1 Mini
  R4 = Resistor [tolerance=±5% resistance=220 package=THT]
  R5 = Resistor [tolerance=±5% resistance=220 package=THT]
  R6 = Resistor [tolerance=±5% resistance=220 package=THT]
  R7 = Resistor [tolerance=±5% resistance=220 package=THT]
  R8 = Resistor [tolerance=±5% resistance=220 package=THT]
  R9 = Resistor [tolerance=±5% resistance=220 package=THT]
  R10 = Resistor [tolerance=±5% resistance=220 package=THT]
  R11 = Resistor [tolerance=±5% resistance=220 package=THT]
  R12 = Resistor [tolerance=±5% resistance=220 package=THT]
  R13 = Resistor [tolerance=±5% resistance=220 package=THT]
  R14 = Resistor [tolerance=±5% resistance=220 package=THT]
  D1 = LED_BARGRAPH_10 [package=led_bargaph_10]
  U1 = 74HC595 [package="DIP16 [THT]"]
  SG2 = Buzzer 12mm [package=buzzer-12mm-ns]

nets (from the breadboard view):
  VCC: RCWL-0516.VDD, 元件1.VCC, C1815.0, WeMos_D1_Mini1.5V, U1.MR, U1.VCC
  N1: RCWL-0516.SIG, WeMos_D1_Mini1.D7, R14.Pin_0
  GND: RCWL-0516.GND, 元件1.GND, S1.3, WeMos_D1_Mini1.G, R4.Pin_0, R5.Pin_0, R6.Pin_0, R7.Pin_0, R8.Pin_0, R9.Pin_0, R10.Pin_0, R11.Pin_0, R12.Pin_0, R13.Pin_0, U1.GND, U1.OE, SG2.2
  N2: 元件1.SDA, WeMos_D1_Mini1.D2
  N3: 元件1.SCL, WeMos_D1_Mini1.D1
  N4: S1.1, WeMos_D1_Mini1.D4
  N5: C1815.2, D1.J_A
  N6: C1815.1, R14.Pin_1
  N7: WeMos_D1_Mini1.D0, U1.DS
  N8: WeMos_D1_Mini1.D3, SG2.1
  N9: WeMos_D1_Mini1.D5, U1.SH_CP
  N10: WeMos_D1_Mini1.D6, D1.I_A
  N11: WeMos_D1_Mini1.D8, U1.ST_CP
  N12: R4.Pin_1, D1.J_C
  N13: R5.Pin_1, D1.I_C
  N14: R6.Pin_1, D1.H_C
  N15: R7.Pin_1, D1.G_C
  N16: R8.Pin_1, D1.F_C
  N17: R9.Pin_1, D1.D_C
  N18: R10.Pin_1, D1.C_C
  N19: R11.Pin_1, D1.B_C
  N20: R12.Pin_1, D1.A_C
  N21: R13.Pin_1, D1.E_C
  N22: D1.A_A, U1.Q7
  N23: D1.B_A, U1.Q6
  N24: D1.C_A, U1.Q5
  N25: D1.D_A, U1.Q4
  N26: D1.E_A, U1.Q3
  N27: D1.F_A, U1.Q2
  N28: D1.G_A, U1.Q1
  N29: D1.H_A, U1.Q0

custom parts:
  LCD1602-I2C: A standard character display, usually with 2x16 characters. Comes in many colors with LCM1602 IIC attached.
